# Fritzing sketch BoxDomotic (saved by Fritzing 0.8.7b)
circuit board: 8.46667cm x 5.64444cm
perfboards: 1

parts:
  Parte1 = Arduino Nano (Rev3.0)
  R1 = Photocell (LDR) [package=THT]
  DS1 = DS18B20 1-Wire Temperature Sensor Probe
  Sensore_PIR_HC-SR502 = HC-SR501 Body Sensor Module
  U1 = 4-Channel 5v Relay Shield [package=relay-4ch5v10a]  # not connected
  U2 = 2-Channel 5v Relay Shield [package=relay-2ch5v10a]  # not connected
  Parte2 = NRF24L01
  R2 = Resistor [tolerance=±5% resistance=220 package=THT]
  R3 = Resistor [tolerance=±5% resistance=220 package=THT]
  R4 = Resistor [tolerance=±5% resistance=220 package=THT]  # not connected
  R5 = Resistor [tolerance=±5% resistance=220 package=THT]  # not connected
  R6 = Photocell (LDR) [package=THT]  # not connected
  DS2 = DS18B20 1-Wire Temperature Sensor Probe  # not connected
  Parte4 = Arduino Nano (Rev3.0)
  J3 = male pin header, 4 pins [form="♂ (male)"]  # not connected
  J4 = male pin header, 4 pins [form="♂ (male)"]  # not connected
  J7 = male pin header, 4 pins [form="♂ (male)"]
  J8 = male pin header, 4 pins [form="♂ (male)"]
  Parte5 = HC-SR501 Body Sensor Module

nets:
  GND: Parte1.GND, DS1.GND, Sensore_PIR_HC-SR502.GND, Parte2.GND, R3.Pin_1
  N1: Parte1.D2, DS1.DQ, R2.Pin_0
  N2: Parte1.D3, Sensore_PIR_HC-SR502.OUT
  N3: Parte1.D9, Parte2.CE
  N4: Parte1.D10, Parte2.CSN
  N5: Parte1.D11/MOSI, Parte2.MOSI
  N6: Parte1.D12/MISO, Parte2.MISO
  5V: Parte1.5V, R1.pin_1, DS1.VDD, Sensore_PIR_HC-SR502.VCC, R2.Pin_1
  N7: Parte1.A7, R1.pin_0, R3.Pin_0
  3V3: Parte1.3V3, Parte2.VCC
  N8: Parte1.D13/SCK, Parte2.SCK
  5V_2: Parte4.5V, J8.pin1, Parte5.VCC
  N9: Parte4.A7, J7.pin2, J8.pin2
  N10: Parte4.A6, J8.pin3
  N11: Parte4.A5, J8.pin4

notes:
  GND&VCC
  from PowerSupply

custom parts:
  HC-SR501 Body Sensor Module: Pyroelectric Infrared PIR Motion Sensor Detector Module
  4-Channel 5v Relay Shield: 4 Channel 5v Relay Shield w. 2x SPD-06VDC-SD-C
  2-Channel 5v Relay Shield: 2 Channel 5v Relay Shield w. 2x SPD-06VDC-SD-C
  HC-SR501 Body Sensor Module: Pyroelectric Infrared PIR Motion Sensor Detector Module
